// Logisim project testbench.circ as structural Verilog: 2 circuits, main circuit IC74181_Test
module IC7447_Test (
);

  wire button_1_out, button_2_out, button_3_out, button_4_out, button_5_out, button_6_out, button_7_out,
       button_8_out, ic7447_1_rbo, ic7447_2_rbo;
  wire [3:0] counter_1_q, counter_2_q, counter_3_q, counter_4_q;
  wire [6:0] ic7447_1_a, ic7447_2_a, ic7447_3_a, ic7447_4_a;

  Button button_1 (.out(button_1_out));
  Button button_2 (.out(button_2_out));
  Button button_3 (.out(button_3_out));
  Button button_4 (.out(button_4_out));
  Button button_5 (.out(button_5_out));
  Button button_6 (.out(button_6_out));
  Button button_7 (.out(button_7_out));
  Button button_8 (.out(button_8_out));
  Counter #(.max('hf), .width(4)) counter_1 (
    .clr(button_1_out), .clk(button_2_out), .Q(counter_1_q));  // open: load, up, count, D, carry
  Counter #(.max('hf), .width(4)) counter_2 (
    .clr(button_3_out), .clk(button_4_out), .Q(counter_2_q));  // open: load, up, count, D, carry
  Counter #(.max('hf), .width(4)) counter_3 (
    .clr(button_5_out), .clk(button_6_out), .Q(counter_3_q));  // open: load, up, count, D, carry
  Counter #(.max('hf), .width(4)) counter_4 (
    .clr(button_7_out), .clk(button_8_out), .Q(counter_4_q));  // open: load, up, count, D, carry
  IC7447 ic7447_1 (
    .d(ic7447_1_a[3]), .e(ic7447_1_a[4]), .f(ic7447_1_a[5]), .g(ic7447_1_a[6]), .a(ic7447_1_a[0]),
    .b(ic7447_1_a[1]), .c(ic7447_1_a[2]), .RBO(ic7447_1_rbo), .Din(counter_1_q[3]), .RBI(1'b0),
    .Ain(counter_1_q[0]), .Bin(counter_1_q[1]), .Cin(counter_1_q[2]));  // open: BI, LT
  IC7447 ic7447_2 (
    .d(ic7447_2_a[3]), .e(ic7447_2_a[4]), .f(ic7447_2_a[5]), .g(ic7447_2_a[6]), .a(ic7447_2_a[0]),
    .b(ic7447_2_a[1]), .c(ic7447_2_a[2]), .RBO(ic7447_2_rbo), .Din(counter_2_q[3]), .RBI(ic7447_1_rbo),
    .Ain(counter_2_q[0]), .Bin(counter_2_q[1]), .Cin(counter_2_q[2]));  // open: BI, LT
  IC7447 ic7447_3 (
    .d(ic7447_3_a[3]), .e(ic7447_3_a[4]), .f(ic7447_3_a[5]), .g(ic7447_3_a[6]), .a(ic7447_3_a[0]),
    .b(ic7447_3_a[1]), .c(ic7447_3_a[2]), .Din(counter_3_q[3]), .RBI(ic7447_2_rbo), .Ain(counter_3_q[0]),
    .Bin(counter_3_q[1]), .Cin(counter_3_q[2]));  // open: RBO, BI, LT
  IC7447 ic7447_4 (
    .d(ic7447_4_a[3]), .e(ic7447_4_a[4]), .f(ic7447_4_a[5]), .g(ic7447_4_a[6]), .a(ic7447_4_a[0]),
    .b(ic7447_4_a[1]), .c(ic7447_4_a[2]), .Din(counter_4_q[3]), .Ain(counter_4_q[0]), .Bin(counter_4_q[1]),
    .Cin(counter_4_q[2]));  // open: RBO, BI, LT, RBI
  _7_Segment_Display #(.active("false"), .decimalPoint("false")) u_7_segment_display_1 (
    .g(ic7447_1_a[6]), .f(ic7447_1_a[5]), .a(ic7447_1_a[0]), .b(ic7447_1_a[1]), .e(ic7447_1_a[4]),
    .d(ic7447_1_a[3]), .c(ic7447_1_a[2]));
  _7_Segment_Display #(.active("false"), .decimalPoint("false")) u_7_segment_display_2 (
    .g(ic7447_2_a[6]), .f(ic7447_2_a[5]), .a(ic7447_2_a[0]), .b(ic7447_2_a[1]), .e(ic7447_2_a[4]),
    .d(ic7447_2_a[3]), .c(ic7447_2_a[2]));
  _7_Segment_Display #(.active("false"), .decimalPoint("false")) u_7_segment_display_3 (
    .g(ic7447_3_a[6]), .f(ic7447_3_a[5]), .a(ic7447_3_a[0]), .b(ic7447_3_a[1]), .e(ic7447_3_a[4]),
    .d(ic7447_3_a[3]), .c(ic7447_3_a[2]));
  _7_Segment_Display #(.active("false"), .decimalPoint("false")) u_7_segment_display_4 (
    .g(ic7447_4_a[6]), .f(ic7447_4_a[5]), .a(ic7447_4_a[0]), .b(ic7447_4_a[1]), .e(ic7447_4_a[4]),
    .d(ic7447_4_a[3]), .c(ic7447_4_a[2]));
endmodule

module IC74181_Test (
  input  B3,
  input  B2,
  input  B1,
  input  B0,
  input  A3,
  input  A2,
  input  A1,
  input  A0
);

  wire ic74181_1_cnp4;
  wire [0:0] not_1_out;
  wire [3:0] ic74181_1_f0;

  IC74181 ic74181_1 (
    .F2(ic74181_1_f0[2]), .F1(ic74181_1_f0[1]), .F0(ic74181_1_f0[0]), .Cnp4(ic74181_1_cnp4),
    .F3(ic74181_1_f0[3]), .B2(B2), .A2(A2), .B1(B1), .A1(A1), .B0(B0), .A0(A0), .M(1'b0), .C_n(1'b1),
    .S3(1'b1), .S2(1'b0), .S1(1'b0), .S0(1'b1), .B3(B3), .A3(A3));  // open: AeqB, G, P
  not not_1 (not_1_out[0], ic74181_1_cnp4);
  Hex_Digit_Display #(.decimalPoint("false")) hex_digit_display_1 (.value({3'b000, not_1_out[0]}));
  Hex_Digit_Display #(.decimalPoint("false")) hex_digit_display_2 (.value(ic74181_1_f0));
endmodule
